# Fritzing sketch parts (saved by Fritzing 0.9.3b)
breadboards: 1

parts:
  U2 = NodeMCU V1.0
  Part2 = RFID-RC522-v2
  OLED1 = OLED 128x64 I2C Monochrome Display
  220V_AC = RELAY-SOLIDSTATE [package=relay-s108t02]  # not connected
  Relay = Keyes Relay [package=THT]
  5V = Power plug

nets:
  N1: U2.D1, OLED1.SCK
  N2: U2.D2, OLED1.SDA
  N3: U2.D4, Part2.SDA
  3V3: U2.3V3, Part2.3.3V, OLED1.VDD, Relay.signal
  GND: U2.GND, Part2.GND, OLED1.GND, Relay.ground, 5V.GND
  N4: U2.D5, Part2.SCK
  N5: U2.D6, Part2.MISO
  N6: U2.D7, Part2.MOSI
  N7: U2.D8, U2.SD3, Relay.power
  VIN: U2.Vin, 5V.VCC
  N8: U2.RST, Part2.RST

custom parts:
  NodeMCU V1.0: ESP8266 based NodeMCU
  RFID-RC522-v2: A simple China made RFID-RC522 Reader; do check the pin labels, as this is a MFRC522 based clone.
  Keyes Relay: The Keyes 5V relay module is suitable for SCM development, home appliance control. It uses a 5V~12V TIL control signal which can control DC / AC signal.
